// Digital circuit Fulladder.dig as structural Verilog
module Fulladder (
  input  ci,
  input  a,
  input  b,
  output s,
  output co
);

  wire halfadderadd_1_c, halfadderadd_1_s, halfadderadd_2_c;

  HalfAdderAdd halfadderadd_1 (.X(a), .Y(b), .S(halfadderadd_1_s), .C(halfadderadd_1_c));
  HalfAdderAdd halfadderadd_2 (.X(ci), .Y(halfadderadd_1_s), .S(s), .C(halfadderadd_2_c));
  or or_1 (co, halfadderadd_2_c, halfadderadd_1_c);
endmodule
