// Digital circuit bb_fulladder.dig as structural Verilog
module bb_fulladder (
  input  ci,
  input  a,
  input  b,
  output s,
  output co
);

  Fulladder fulladder_1 (.ci(ci), .a(a), .b(b), .s(s), .co(co));
endmodule

/* Test case testbench:
	a	b	ci	co	s
loop(x,8)
	bits(3,x)	bits(2,(x>>0&1) + (x>>1&1) + (x>>2&1))
end loop
*/
