// Digital circuit sumrest.dig as structural Verilog
module sumrest (
  input  b3,
  input  a3,
  input  b2,
  input  a2,
  input  b1,
  input  a1,
  input  b0,
  input  a0,
  input  Sh,
  output s0,
  output s1,
  output s2,
  output s3,
  output Co
);

  wire add_1_c_o, add_1_s, add_2_c_o, add_2_s, add_3_c_o, add_3_s, add_4_c_o, add_4_s, xor_2_out, xor_4_out,
       xor_6_out, xor_8_out;

  xor xor_1 (Co, Sh, add_1_c_o);
  Add add_1 (.a(a3), .b(xor_2_out), .c_i(add_2_c_o), .s(add_1_s), .c_o(add_1_c_o));
  xor xor_2 (xor_2_out, Sh, b3);
  xor xor_3 (s3, Sh, add_1_s);
  Add add_2 (.a(a2), .b(xor_4_out), .c_i(add_3_c_o), .s(add_2_s), .c_o(add_2_c_o));
  xor xor_4 (xor_4_out, Sh, b2);
  xor xor_5 (s2, Sh, add_2_s);
  Add add_3 (.a(a1), .b(xor_6_out), .c_i(add_4_c_o), .s(add_3_s), .c_o(add_3_c_o));
  xor xor_6 (xor_6_out, Sh, b1);
  xor xor_7 (s1, Sh, add_3_s);
  Add add_4 (.a(a0), .b(xor_8_out), .c_i(Sh), .s(add_4_s), .c_o(add_4_c_o));
  xor xor_8 (xor_8_out, Sh, b0);
  xor xor_9 (s0, Sh, add_4_s);
endmodule
